# Fritzing sketch wiring-diagram_bb (saved by Fritzing 0.9.4)

parts:
  Part1 = Arduino Nano (Rev3.0)  # not connected
  HC-SR04_Sensor_1 = HC-SR04 Ultrasonic Distance Sensor
  Part2 = Bluetooth HM-10
  Mod1 = Nano-V3-0-IO-Expansion-Adapter
  M1 = Dagu DGServo 9g (Top view) [part_number=RS001B]
  M2 = Dagu DGServo 9g (Top view) [part_number=RS001B]
  M3 = Dagu DGServo 9g (Top view) [part_number=RS001B]
  M4 = Dagu DGServo 9g (Top view) [part_number=RS001B]
  M5 = Dagu DGServo 9g (Top view) [part_number=RS001B]
  M6 = Dagu DGServo 9g (Top view) [part_number=RS001B]
  M7 = Dagu DGServo 9g (Top view) [part_number=RS001B]
  M8 = Dagu DGServo 9g (Top view) [part_number=RS001B]

nets:
  VCC: HC-SR04_Sensor_1.VCC, HC-SR04_Sensor_1.ECHO, Mod1.VCC, Mod1.D3_PWM, M1.vcc, M2.vcc, M3.vcc, M4.vcc, M5.vcc, M6.vcc, M7.vcc, M8.vcc
  N1: HC-SR04_Sensor_1.TRIG, Mod1.D2
  GND: HC-SR04_Sensor_1.GND, Mod1.GND, M1.gnd, M2.gnd, M3.gnd, M4.gnd, M5.gnd, M6.gnd, M7.gnd, M8.gnd
  N2: Part2.RXD, Mod1.D13/SCK
  N3: Part2.TXD, Mod1.D12/MISO
  N4: Part2.GND, Mod1.D1/TX
  N5: Part2.VCC, Mod1.D0/RX
  N6: Mod1.D11_PWM/MOSI, M8.pulse
  N7: Mod1.D10_PWM/SS, M7.pulse
  N8: Mod1.D9_PWM, M6.pulse
  N9: Mod1.D8, M5.pulse
  N10: Mod1.D7, M2.pulse
  N11: Mod1.D6_PWM, M1.pulse
  N12: Mod1.D5_PWM, M4.pulse
  N13: Mod1.D4, M3.pulse

custom parts:
  Nano-V3-0-IO-Expansion-Adapter: Nano V3.0 IO Expansion Adapter Shield. Note pcb view has been supressed as not useful. You can drag a Nano over the Nano connectors and it will connect and appear in schematic (although at present due to a bug, routing will not show as complete in breadboard).
